# Fritzing sketch sheme (saved by Fritzing 0.9.3b)
stripboards: 1

parts:
  Часть1 = Arduino Nano (Rev3.0)
  Button = Pushbutton [package="[THT]"]
  Power_plug_12VDC = Power plug
  C1 = Ceramic Capacitor [capacitance=100nF package="100 mil [THT, multilayer]"]
  Dimmer_control = male pin header, 2 pins [form="♂ (male)" part_number="GND, 10VDC"]
  PN2222A = NPN-Transistor [package="TO92 [THT]"]
  R1 = Resistor [tolerance=±5% resistance=10k package=THT]
  R2 = Resistor [tolerance=±5% resistance=10k package=THT]
  HTU21D_interface = male pin header, 4 pins [form="♂ (male)" part_number="SDA, SCL, GND, +3.3V"]
  R3 = Resistor [tolerance=±5% resistance=10k package=THT]

nets:
  GND: Часть1.GND, Button.Pin_1, Button.Pin_2, Power_plug_12VDC.GND, C1.1, Dimmer_control.pin2, PN2222A.E, HTU21D_interface.pin2
  N1: Часть1.D2, Button.Pin_3, Button.Pin_4, C1.0, R3.Pin_0
  N2: Часть1.D3, R1.Pin_0, R2.Pin_0
  VIN: Часть1.VIN, Power_plug_12VDC.VCC
  N3: Часть1.5V, R1.Pin_1, R3.Pin_1
  N4: Часть1.A5, HTU21D_interface.pin3
  N5: Часть1.A4, HTU21D_interface.pin4
  N6: Часть1.3V3, HTU21D_interface.pin1
  N7: Dimmer_control.pin1, PN2222A.C
  N8: PN2222A.B, R2.Pin_1
